// Logisim project  Nand  as universal.circ as structural Verilog: 1 circuit, main circuit main
module main (
  input  in_1,
  input  A,
  input  B,
  input  A_2,
  input  B_2,
  output A_prime,
  output AB,
  output out_8
);

  wire nand_2_out, nand_3_out, nand_4_out;

  nand nand_1 (A_prime, in_1, in_1);
  nand nand_2 (nand_2_out, A, B);
  nand nand_3 (nand_3_out, A_2, A_2);
  nand nand_4 (nand_4_out, B_2, B_2);
  nand nand_5 (AB, nand_2_out, nand_2_out);
  nand nand_6 (out_8, nand_3_out, nand_4_out);

  // Notes on the sheet:
  //   A
  //   (AB)' 
  //   A'
  //   B'
  //   A+B
endmodule
