// Logisim project Nor as universal.circ as structural Verilog: 1 circuit, main circuit main
module main (
  input  A,
  input  A_2,
  input  B,
  input  A_3,
  input  B_2,
  output A_prime,
  output out_7,
  output A_B
);

  wire nor_2_out, nor_3_out, nor_4_out;

  nor nor_1 (A_prime, A, A);
  nor nor_2 (nor_2_out, A_2, A_2);
  nor nor_3 (nor_3_out, B, B);
  nor nor_4 (nor_4_out, A_3, B_2);
  nor nor_5 (out_7, nor_2_out, nor_3_out);
  nor nor_6 (A_B, nor_4_out, nor_4_out);

  // Notes on the sheet:
  //   A'
  //   B'
  //   A'+B'
  //   AB
endmodule
