// Logisim project taks 3 in IC.circ as structural Verilog: 4 circuits, main circuit main
module main (
  input  in_1,
  input  in_2,
  input  in_3,
  output F
);

  wire and_ic_1_out_9, and_ic_2_out_9, not_ic_1_out_10;

  Not_ic not_ic_1 (
    .in_4(in_3), .out_10(not_ic_1_out_10));  // open: in_1, in_2, in_3, in_5, in_6, out_7, out_8, out_9, out_11, out_12
  And_ic and_ic_1 (
    .in_1(in_3), .in_2(in_1), .out_9(and_ic_1_out_9));  // open: in_3, in_4, in_5, in_6, in_7, in_8, out_10, out_11, out_12
  And_ic and_ic_2 (
    .in_1(in_2), .in_2(not_ic_1_out_10), .out_9(and_ic_2_out_9));  // open: in_3, in_4, in_5, in_6, in_7, in_8, out_10, out_11, out_12
  or_ic or_ic_1 (
    .in_1(and_ic_1_out_9), .in_2(and_ic_2_out_9), .out_9(F));  // open: in_3, in_4, in_5, in_6, in_7, in_8, out_10, out_11, out_12

  // Notes on the sheet:
  //   A
  //   B
  //   C
endmodule

module Not_ic (
  input  in_1,
  input  in_2,
  input  in_3,
  input  in_4,
  input  in_5,
  input  in_6,
  output out_7,
  output out_8,
  output out_9,
  output out_10,
  output out_11,
  output out_12
);

  not not_1 (out_7, in_1);
  not not_2 (out_8, in_2);
  not not_3 (out_9, in_3);
  not not_4 (out_10, in_4);
  not not_5 (out_11, in_5);
  not not_6 (out_12, in_6);
endmodule

module And_ic (
  input  in_1,
  input  in_2,
  input  in_3,
  input  in_4,
  input  in_5,
  input  in_6,
  input  in_7,
  input  in_8,
  output out_9,
  output out_10,
  output out_11,
  output out_12
);

  and and_1 (out_9, in_1, in_2);
  and and_2 (out_10, in_3, in_4);
  and and_3 (out_11, in_5, in_6);
  and and_4 (out_12, in_7, in_8);
endmodule

module or_ic (
  input  in_1,
  input  in_2,
  input  in_3,
  input  in_4,
  input  in_5,
  input  in_6,
  input  in_7,
  input  in_8,
  output out_9,
  output out_10,
  output out_11,
  output out_12
);

  or or_1 (out_9, in_1, in_2);
  or or_2 (out_10, in_3, in_4);
  or or_3 (out_11, in_5, in_6);
  or or_4 (out_12, in_7, in_8);
endmodule
