// Logisim project IC.circ as structural Verilog: 4 circuits, main circuit main
module main (
  input  W,
  input  in_2,
  input  in_3,
  input  Z,
  output out_5,
  output B_X_prime_Z_X_prime_Y_XY_prime_Z,
  output out_7
);

  wire ic_7404_1_out_8, ic_7404_1_out_9, ic_7404_1_out_10, ic_7404_1_out_11, ic_7404_1_out_12,
       ic_7411_1_out_13, ic_7411_1_out_14, ic_7411_1_out_15, ic_7411_1_out_16, ic_7411_2_out_15;

  IC_7404 ic_7404_1 (
    .in_2(W), .in_3(in_2), .in_4(ic_7411_2_out_15), .in_5(Z), .in_6(in_3), .out_8(ic_7404_1_out_8),
    .out_9(ic_7404_1_out_9), .out_10(ic_7404_1_out_10), .out_11(ic_7404_1_out_11), .out_12(ic_7404_1_out_12));  // open: in_1, out_7
  IC_7411 ic_7411_1 (
    .in_1(in_2), .in_2(Z), .in_4(in_2), .in_5(in_3), .in_7(Z), .in_8(ic_7404_1_out_9),
    .out_13(ic_7411_1_out_13), .out_14(ic_7411_1_out_14), .out_15(ic_7411_1_out_15), .in_10(ic_7404_1_out_9),
    .in_11(in_3), .out_16(ic_7411_1_out_16));  // open: in_3, in_6, in_9, in_12
  IC_7411 ic_7411_2 (
    .in_1(in_2), .in_2(ic_7404_1_out_12), .in_3(ic_7404_1_out_11), .in_7(Z), .in_8(in_3),
    .out_13(ic_7411_1_out_16), .out_15(ic_7411_2_out_15));  // open: in_4, in_5, in_6, in_9, out_14, in_10, in_11, out_16, in_12
  IC_7432 ic_7432_1 (
    .in_1(ic_7411_1_out_13), .in_3(ic_7411_1_out_14), .in_4(ic_7411_1_out_15), .in_6(ic_7411_1_out_16),
    .in_10(ic_7404_1_out_10), .in_12(ic_7411_2_out_15), .out_13(out_5),
    .out_14(B_X_prime_Z_X_prime_Y_XY_prime_Z), .out_16(out_7), .in_2(W), .in_5(ic_7411_1_out_16));  // open: in_7, in_9, out_15, in_8, in_11

  // Notes on the sheet:
  //   X
  //   Y
  //   X'
  //   Y'
  //   W'
  //   Z'
  //   Y'Z'
  //   XZ
  //   XY
  //   X'Z
  //   X'Y
  //   XY'Z'
  //   YZ
  //   C= Y'Z' +YZ
  //   A=W+XZ+XY
endmodule

module IC_7411 (
  input  in_1,
  input  in_2,
  input  in_3,
  input  in_4,
  input  in_5,
  input  in_6,
  input  in_7,
  input  in_8,
  input  in_9,
  input  in_10,
  input  in_11,
  input  in_12,
  output out_13,
  output out_14,
  output out_15,
  output out_16
);

  and and_1 (out_13, in_1, in_2, in_3);
  and and_2 (out_14, in_4, in_5, in_6);
  and and_3 (out_15, in_7, in_8, in_9);
  and and_4 (out_16, in_10, in_11, in_12);
endmodule

module IC_7404 (
  input  in_1,
  input  in_2,
  input  in_3,
  input  in_4,
  input  in_5,
  input  in_6,
  output out_7,
  output out_8,
  output out_9,
  output out_10,
  output out_11,
  output out_12
);

  not not_1 (out_7, in_1);
  not not_2 (out_8, in_2);
  not not_3 (out_9, in_3);
  not not_4 (out_10, in_4);
  not not_5 (out_11, in_5);
  not not_6 (out_12, in_6);
endmodule

module IC_7432 (
  input  in_1,
  input  in_2,
  input  in_3,
  input  in_4,
  input  in_5,
  input  in_6,
  input  in_7,
  input  in_8,
  input  in_9,
  input  in_10,
  input  in_11,
  input  in_12,
  output out_13,
  output out_14,
  output out_15,
  output out_16
);

  or or_1 (out_13, in_1, in_2, in_3);
  or or_2 (out_14, in_4, in_5, in_6);
  or or_3 (out_15, in_7, in_8, in_9);
  or or_4 (out_16, in_10, in_11, in_12);
endmodule
